# Fritzing sketch Motor Elektrisch Design (saved by Fritzing 0.9.3b)
breadboards: 1

parts:
  part = Arduino Uno (Rev3)
  1A = DC Power [voltage=9V]
  M1 = Stepper Motor - Bipolar
  M2 = Stepper Motor - Bipolar
  Stepper_driver_M1 = DRV 8825 Stepper Motor Carrier, High Current [part_number="DRV 8825"]
  Stepper_driver_M2 = DRV 8825 Stepper Motor Carrier, High Current [part_number="DRV 8825"]
  100µF_Capacitor = Capacitor Polarized [package=cpol-radial-100uf-25v]
  100µF_Capacitor_2 = Capacitor Polarized [package=cpol-radial-100uf-25v]
  2A = DC Power [voltage=5V]
  DIP_Switch_2x3 = DIP Switch 8 Position [package=dipswitch-08]

nets:
  N1: part.GND, 1A.V-, Stepper_driver_M1.ENABLE, Stepper_driver_M1.GROUND_ST/_MT, Stepper_driver_M1.GROUND_LOG, Stepper_driver_M2.ENABLE, Stepper_driver_M2.GROUND_ST/_MT, Stepper_driver_M2.GROUND_LOG, 100µF_Capacitor.-, 100µF_Capacitor_2.-, 2A.V-
  N2: part.D3_PWM, Stepper_driver_M1.STEP
  N3: part.D4, Stepper_driver_M1.DIRECTION
  N4: part.D5_PWM, Stepper_driver_M2.STEP
  N5: part.D6_PWM, Stepper_driver_M2.DIRECTION
  N6: part.5V, Stepper_driver_M1.VOLTAGE_DD, Stepper_driver_M2.VOLTAGE_DD, DIP_Switch_2x3.1, DIP_Switch_2x3.2, DIP_Switch_2x3.3, DIP_Switch_2x3.6, DIP_Switch_2x3.7, DIP_Switch_2x3.8
  N7: part.VIN, 2A.V+
  N8: 1A.V+, Stepper_driver_M1.VOLTAGE_ST/_MT, Stepper_driver_M2.VOLTAGE_ST/_MT, 100µF_Capacitor.+, 100µF_Capacitor_2.+
  N9: M1.A, Stepper_driver_M1.OUT_2A
  N10: M1.C, Stepper_driver_M1.OUT_2B
  N11: M1.B, Stepper_driver_M1.OUT_1A
  N12: M1.D, Stepper_driver_M1.OUT_1B
  N13: M2.A, Stepper_driver_M2.OUT_2A
  N14: M2.C, Stepper_driver_M2.OUT_2B
  N15: M2.B, Stepper_driver_M2.OUT_1A
  N16: M2.D, Stepper_driver_M2.OUT_1B
  N17: Stepper_driver_M1.MS1, DIP_Switch_2x3.14
  N18: Stepper_driver_M1.MS2, DIP_Switch_2x3.15
  N19: Stepper_driver_M1.MS3, DIP_Switch_2x3.16
  N20: Stepper_driver_M1.RESET, Stepper_driver_M1.SLEEP
  N21: Stepper_driver_M2.MS1, DIP_Switch_2x3.9
  N22: Stepper_driver_M2.MS2, DIP_Switch_2x3.10
  N23: Stepper_driver_M2.MS3, DIP_Switch_2x3.11
  N24: Stepper_driver_M2.RESET, Stepper_driver_M2.SLEEP
